# Fritzing sketch Untitled Sketch 2 (saved by Fritzing 0.9.3b)
breadboards: 2
perfboards: 1

parts:
  M2 = fc-51 [package=THT]
  M3 = fc-51 [package=THT]
  S1 = Round Pushbutton
  Conductivity_Circuit1 = Conductivity Circuit  # not connected
  WeMos_D1_Mini1 = WeMos D1 Mini
  A1 = WS2811 LED strip  # not connected
  A2 = WS2811 LED strip
  A3 = WS2811 LED strip  # not connected
  A4 = WS2811 LED strip
  WeMos_D1_Mini2 = WeMos D1 Mini  # not connected
  M4 = fc-51 [package=THT]  # not connected
  M5 = fc-51 [package=THT]  # not connected
  A5 = WS2811 LED strip  # not connected
  A6 = WS2811 LED strip  # not connected

nets:
  N1: M2.pin1, WeMos_D1_Mini1.D4
  N2: M2.pin2, M3.pin2, S1.leg1, WeMos_D1_Mini1.G, A2.Pin_3, A2.Pin_4, A4.Pin_4
  N3: M2.pin3, M3.pin3, WeMos_D1_Mini1.5V, A2.Pin_1, A2.Pin_6, A4.Pin_6
  N4: M3.pin1, WeMos_D1_Mini1.D5
  N5: S1.leg0, WeMos_D1_Mini1.D2
  N6: WeMos_D1_Mini1.D6, A4.Pin_5
  N7: WeMos_D1_Mini1.D7, A2.Pin_5
